# Fritzing sketch ShoeFlasher (saved by Fritzing 0.9.2b)

parts:
  U1 = attiny85 [package=dip]
  LED1 = RGB LED (com. cathode, rbg) [part_number=RGB5050 package="5 mm [THT]"]
  S1 = Tilt Switch [part_number=SW-18020P package=THT]
  BAT1 = Battery Holders [part_number=CR2032 package=battery_20mm_pth_compact]

nets:
  N1: U1.Pin_2, LED1.green_anode
  N2: U1.Pin_4, LED1.common_cathode, S1.Pin_2, BAT1.-
  N3: U1.Pin_5, LED1.red_anode
  N4: U1.Pin_6, LED1.blue_anode
  N5: U1.Pin_7, S1.Pin_1
  N6: U1.Pin_8, BAT1.+
